// Logisim project 1.circ as structural Verilog
module LAB1_2_1 (
  input  CLK,
  input  CLR,
  input  WR,
  input  RD
);

  wire keyboard_1_avail;
  wire [6:0] keyboard_1_data;

  TTY tty_1 (.data(keyboard_1_data), .clk(CLK), .we(WR), .clr(CLR));
  Keyboard keyboard_1 (.clk(CLK), .re(RD), .clr(CLR), .avail(keyboard_1_avail), .data(keyboard_1_data));
  // Probe on keyboard_1_avail
  // Probe on keyboard_1_data
endmodule

module LAB3_2 (
  input  CLK,
  input  CLR,
  input  WR,
  input  RD,
  input  B_nK,
  input  [6:0] BINARY
);

  wire keyboard_1_avail;
  wire [6:0] keyboard_1_data, multiplexer_1_out;

  TTY tty_1 (.data(multiplexer_1_out), .clk(CLK), .we(WR), .clr(CLR));
  Keyboard keyboard_1 (.clk(CLK), .re(RD), .clr(CLR), .avail(keyboard_1_avail), .data(keyboard_1_data));
  // Probe on keyboard_1_avail
  // Probe on keyboard_1_data
  Multiplexer #(.width(7), .enable("false")) multiplexer_1 (
    .in0(keyboard_1_data), .in1(BINARY), .out(multiplexer_1_out), .sel(B_nK));
endmodule
