// Logisim project 2.circ as structural Verilog
module _1_1 (
  input  A,
  input  B,
  input  A_2,
  input  B_2,
  input  A_3,
  input  B_3,
  output AB,
  output A_B,
  output A_xor_B
);

  and and_1 (AB, A, B);
  or or_1 (A_B, A_2, B_2);
  xor xor_1 (A_xor_B, A_3, B_3);
endmodule

module _1_2 (
  input  A,
  input  A_2,
  input  B,
  input  A_3,
  input  B_2,
  input  A_4,
  input  B_3,
  output nA,
  output AB,
  output A_B,
  output n_A_xor_B
);

  not not_1 (nA, A);
  nand nand_1 (AB, A_2, B);
  nor nor_1 (A_B, A_3, B_2);
  xnor xnor_1 (n_A_xor_B, A_4, B_3);
endmodule

module _1_3 (
  input  A,
  input  B,
  input  C,
  input  A_2,
  input  B_2,
  input  C_2,
  input  A_3,
  input  B_3,
  input  C_3,
  output ABC,
  output ABC_2,
  output ABC_3
);

  wire and_1_out, and_2_out;

  and and_1 (and_1_out, A, B);
  and and_2 (and_2_out, B_2, C_2);
  and and_3 (ABC_3, A_3, B_3, C_3);
  and and_4 (ABC, and_1_out, C);
  and and_5 (ABC_2, A_2, and_2_out);
endmodule

module _1_4 (
  input  A,
  input  B,
  input  C,
  input  A_2,
  input  B_2,
  input  C_2,
  input  A_3,
  input  B_3,
  input  C_3,
  input  A_4,
  input  B_4,
  input  C_4,
  output F0,
  output F1,
  output F2,
  output F3
);

  wire and_1_out, and_3_out, and_4_out, or_1_out, or_2_out, or_3_out;

  or or_1 (or_1_out, A, B);
  and and_1 (and_1_out, A_3, B_3);
  or or_2 (or_2_out, A_4, C_4);
  or or_3 (or_3_out, B_4, C_4);
  and and_2 (F0, or_1_out, C);
  and and_3 (and_3_out, A_2, C_2);
  and and_4 (and_4_out, B_2, C_2);
  or or_4 (F2, and_1_out, C_3);
  and and_5 (F3, or_2_out, or_3_out);
  or or_5 (F1, and_3_out, and_4_out);
endmodule

module _1 (
  input  A,
  input  B,
  input  A_2,
  input  B_2,
  input  A_3,
  input  B_3,
  input  A_4,
  input  B_4,
  output F0,
  output F1,
  output F2,
  output F3
);

  wire not_1_out, not_2_out;

  nor nor_1 (F0, A, B);
  not not_1 (not_1_out, A_2);
  and and_1 (F1, not_1_out, not_2_out);
  not not_2 (not_2_out, B_2);
  nand nand_1 (F2, A_3, B_3);
  or or_1 (F3, ~A_4, ~B_4);  // OR_Gate
endmodule

module _2_1 (
  input  A,
  input  A_2,
  input  B,
  input  B_2,
  input  C,
  input  C_2,
  input  A_3,
  input  B_3,
  input  C_3,
  input  A_4,
  input  B_4,
  input  C_4,
  output AB_nAC,
  output AB___nAC___BC,
  output nA_nB___AB_nC,
  output out_16
);

  wire and_1_out, and_2_out, and_3_out, and_4_out, and_5_out, and_6_out, and_7_out, and_8_out, and_9_out,
       and_10_out, and_11_out, not_1_out, not_2_out, not_3_out, not_4_out, not_5_out, not_6_out, not_7_out,
       not_8_out, not_9_out, or_1_out, or_2_out;

  not not_1 (not_1_out, A);
  and and_1 (and_1_out, A, B_2);
  and and_2 (and_2_out, not_1_out, C_2);
  and and_3 (and_3_out, C_2, B_2);
  and and_4 (and_4_out, A_4, C_4);
  not not_2 (not_2_out, B_4);
  and and_5 (and_5_out, B_4, not_3_out);
  not not_3 (not_3_out, C_4);
  and and_6 (and_6_out, A_4, B_4, not_4_out);
  not not_4 (not_4_out, C_4);
  or or_1 (or_1_out, and_4_out, not_2_out);
  not not_5 (not_5_out, or_2_out);
  or or_2 (or_2_out, A_4, and_5_out);
  or or_3 (AB___nAC___BC, and_1_out, and_2_out, and_3_out);
  and and_7 (and_7_out, or_1_out, not_5_out);
  or or_4 (out_16, and_7_out, and_6_out);
  not not_6 (not_6_out, A_2);
  and and_8 (and_8_out, A_2, B);
  and and_9 (and_9_out, not_6_out, C);
  not not_7 (not_7_out, A_3);
  and and_10 (and_10_out, not_7_out, not_8_out);
  not not_8 (not_8_out, B_3);
  and and_11 (and_11_out, A_3, B_3, not_9_out);
  not not_9 (not_9_out, C_3);
  or or_5 (AB_nAC, and_8_out, and_9_out);
  or or_6 (nA_nB___AB_nC, and_10_out, and_11_out);

  // Notes on the sheet:
  //   (~B + AC)~(A+B~C)+AB~C
endmodule

module _2_2 (
  input  A,
  input  B,
  input  C,
  input  A_2,
  input  B_2,
  input  C_2,
  output out_7,
  output out_8
);

  wire and_1_out, and_2_out, and_3_out, and_4_out, not_1_out, not_2_out, not_3_out, or_1_out, or_2_out,
       or_3_out;

  not not_1 (not_1_out, A_2);
  not not_2 (not_2_out, B_2);
  not not_3 (not_3_out, C_2);
  or or_1 (or_1_out, A, and_1_out);
  and and_1 (and_1_out, B, C);
  or or_2 (or_2_out, B, and_2_out);
  and and_2 (and_2_out, A, C);
  or or_3 (or_3_out, not_2_out, not_3_out);
  and and_3 (and_3_out, not_2_out, not_3_out);
  and and_4 (and_4_out, not_1_out, or_3_out);
  or or_4 (out_8, and_4_out, and_3_out);
  nand nand_1 (out_7, or_1_out, or_2_out);

  // Notes on the sheet:
  //   ~((A+BC)(AC+B))
  //   ~A(~B+~C)+~B~C
endmodule

module _3_1 (
  input  A,
  input  B,
  output S,
  output C
);

  wire nand_1_out, nand_2_out, nand_3_out;

  nand nand_1 (nand_1_out, A, B);
  nand nand_2 (nand_2_out, A, nand_1_out);
  nand nand_3 (nand_3_out, nand_1_out, B);
  nand nand_4 (S, nand_2_out, nand_3_out);
  and and_1 (C, A, B);
endmodule

module _3_2 (
  input  A,
  input  B,
  input  C,
  output S,
  output Co
);

  wire and_1_out, and_2_out, xor_1_out;

  xor xor_1 (xor_1_out, A, B);
  and and_1 (and_1_out, A, B);
  xor xor_2 (S, xor_1_out, C);
  or or_1 (Co, and_1_out, and_2_out);
  and and_2 (and_2_out, xor_1_out, C);
endmodule
