// Logisim project 3.circ as structural Verilog
module _1_2_1 (
  input  A,
  input  B,
  input  C,
  output F_BC_AC_AB
);

  wire and_1_out, and_2_out, and_3_out, or_1_out;

  and and_1 (and_1_out, A, B);
  and and_2 (and_2_out, A, C);
  and and_3 (and_3_out, B, C);
  or or_1 (or_1_out, and_1_out, and_2_out);
  or or_2 (F_BC_AC_AB, or_1_out, and_3_out);
endmodule

module _1_2_2 (
  input  B3,
  input  B2,
  input  B1,
  input  B0,
  output F2,
  output F1,
  output F0
);

  wire and_1_out, and_2_out, and_3_out, and_4_out, and_5_out, not_1_out, not_2_out, not_3_out, not_4_out,
       or_1_out, xor_1_out, xor_2_out;

  not not_1 (not_1_out, B3);
  not not_2 (not_2_out, B2);
  not not_3 (not_3_out, B1);
  not not_4 (not_4_out, B0);
  or or_1 (or_1_out, B1, B0);
  xor xor_1 (xor_1_out, B3, B2);
  and and_1 (and_1_out, B3, not_2_out);
  and and_2 (and_2_out, not_1_out, B0, B1);
  and and_3 (and_3_out, B3, not_3_out, not_4_out);
  xor xor_2 (xor_2_out, B0, B1);
  and and_4 (and_4_out, B2, and_2_out);
  and and_5 (and_5_out, xor_2_out, not_2_out);
  and and_6 (F2, B3, B2, or_1_out);
  or or_2 (F1, xor_1_out, and_2_out, and_3_out);
  or or_3 (F0, and_1_out, and_4_out, and_3_out, and_5_out);

  // Notes on the sheet:
  //   X
  //   Y
endmodule

module _1_2_3 (
  input  A2,
  input  A1,
  input  A0,
  output F7,
  output F6,
  output F5,
  output F4,
  output F3,
  output F2,
  output F1,
  output F0
);

  wire not_1_out, not_2_out, not_3_out;

  not not_1 (not_1_out, A2);
  not not_2 (not_2_out, A1);
  not not_3 (not_3_out, A0);
  and and_1 (F7, A2, A1, A0);
  and and_2 (F6, A2, A1, not_3_out);
  and and_3 (F5, A2, not_2_out, A0);
  and and_4 (F4, A2, not_2_out, not_3_out);
  and and_5 (F3, not_1_out, A1, A0);
  and and_6 (F2, not_1_out, A1, not_3_out);
  and and_7 (F1, not_1_out, not_2_out, A0);
  and and_8 (F0, not_1_out, not_2_out, not_3_out);
endmodule

module _1_2_4 (
  input  LT,
  input  RT,
  input  BR,
  input  EM
);

  wire and_1_out, and_2_out, and_3_out, clock_1_out, not_1_out, or_1_out, or_2_out, or_3_out, or_4_out,
       or_5_out, xor_1_out, xor_2_out;

  Clock clock_1 (.out(clock_1_out));
  not not_1 (not_1_out, BR);
  or or_1 (or_1_out, BR, EM);
  and and_1 (and_1_out, not_1_out, EM);
  or or_2 (or_2_out, LT, or_1_out);
  or or_3 (or_3_out, RT, or_1_out);
  or or_4 (or_4_out, LT, and_1_out);
  or or_5 (or_5_out, and_1_out, RT);
  and and_2 (and_2_out, or_4_out, clock_1_out);
  and and_3 (and_3_out, or_5_out, clock_1_out);
  xor xor_1 (xor_1_out, or_2_out, and_2_out);
  xor xor_2 (xor_2_out, or_3_out, and_3_out);
  LED led_1 (.in(xor_1_out));
  LED led_2 (.in(xor_2_out));

  // Notes on the sheet:
  //   BL
  //   X
  //   Y
  //   LR0
  //   RR0
  //   LBL
  //   RBL
  //   LR
  //   RR
endmodule

module _1_2_5 (
  input  C0,
  input  A3,
  input  A2,
  input  A1,
  input  A0,
  input  B3,
  input  B2,
  input  B1,
  input  B0,
  output C,
  output F3,
  output F2,
  output F1,
  output F0
);

  wire and_1_out, and_2_out, and_3_out, and_4_out, and_5_out, and_6_out, and_7_out, and_8_out, or_1_out,
       or_2_out, or_3_out, xor_1_out, xor_3_out, xor_5_out, xor_7_out;

  xor xor_1 (xor_1_out, A0, B0);
  and and_1 (and_1_out, B0, A0);
  xor xor_2 (F0, xor_1_out, C0);
  and and_2 (and_2_out, xor_1_out, C0);
  or or_1 (or_1_out, and_1_out, and_2_out);
  xor xor_3 (xor_3_out, A1, B1);
  and and_3 (and_3_out, B1, A1);
  xor xor_4 (F1, xor_3_out, or_1_out);
  and and_4 (and_4_out, xor_3_out, or_1_out);
  or or_2 (or_2_out, and_3_out, and_4_out);
  xor xor_5 (xor_5_out, A2, B2);
  and and_5 (and_5_out, B2, A2);
  xor xor_6 (F2, xor_5_out, or_2_out);
  and and_6 (and_6_out, xor_5_out, or_2_out);
  or or_3 (or_3_out, and_5_out, and_6_out);
  xor xor_7 (xor_7_out, A3, B3);
  and and_7 (and_7_out, B3, A3);
  xor xor_8 (F3, xor_7_out, or_3_out);
  and and_8 (and_8_out, xor_7_out, or_3_out);
  or or_4 (C, and_7_out, and_8_out);

  // Notes on the sheet:
  //   +
endmodule
