// Logisim project 4.circ as structural Verilog
module _1_2_1 (
  input  [3:0] B3
);

  wire and_1_out, and_2_out, and_3_out, and_4_out, and_5_out, and_6_out, and_7_out, not_1_out, not_2_out,
       not_3_out, not_4_out, not_5_out, or_1_out, or_2_out, or_3_out, or_4_out, or_5_out, or_6_out, or_7_out,
       xor_1_out, xor_2_out, xor_3_out;

  not not_1 (not_1_out, B3[2]);
  not not_2 (not_2_out, B3[1]);
  not not_3 (not_3_out, B3[0]);
  and and_1 (and_1_out, B3[2], not_2_out);
  and and_2 (and_2_out, not_3_out, B3[1]);
  and and_3 (and_3_out, not_3_out, not_1_out);
  xor xor_1 (xor_1_out, B3[0], B3[1]);
  xor xor_2 (xor_2_out, B3[0], B3[2]);
  and and_4 (and_4_out, not_3_out, B3[2]);
  and and_5 (and_5_out, not_3_out, not_2_out);
  not not_4 (not_4_out, xor_1_out);
  not not_5 (not_5_out, xor_2_out);
  xor xor_3 (xor_3_out, B3[1], B3[2]);
  and and_6 (and_6_out, not_1_out, B3[1]);
  and and_7 (and_7_out, and_1_out, B3[0]);
  or or_1 (or_1_out, B3[3], not_1_out, not_4_out);
  or or_2 (or_2_out, B3[3], B3[1], not_5_out);
  or or_3 (or_3_out, B3[3], and_4_out, and_1_out, and_5_out);
  or or_4 (or_4_out, B3[3], and_2_out, xor_3_out);
  or or_5 (or_5_out, B3[0], B3[3], B3[2], not_2_out);
  or or_6 (or_6_out, and_3_out, and_2_out);
  or or_7 (or_7_out, and_2_out, B3[3], and_6_out, and_7_out, and_3_out);
  _7_Segment_Display u_7_segment_display_1 (
    .g(or_4_out), .f(or_3_out), .a(or_2_out), .b(or_1_out), .e(or_6_out), .d(or_7_out), .c(or_5_out));  // open: dp

  // Notes on the sheet:
  //   B2
  //   B1
  //   Z
  //   X
  //   Y
  //   B0
  //   F0
  //   F1
  //   F2
  //   F3
  //   F4
  //   F5
  //   F6
endmodule

module _1_2_2 (
  input  [3:0] A,
  input  [3:0] B,
  input  SEL,
  output [3:0] M
);

  wire not_1_out;
  wire [3:0] and_1_out, and_5_out;

  not not_1 (not_1_out, SEL);
  and and_1 (and_1_out[0], A[0], not_1_out);
  and and_2 (and_1_out[1], A[1], not_1_out);
  and and_3 (and_1_out[2], A[2], not_1_out);
  and and_4 (and_1_out[3], A[3], not_1_out);
  and and_5 (and_5_out[0], B[0], SEL);
  and and_6 (and_5_out[1], B[1], SEL);
  and and_7 (and_5_out[2], B[2], SEL);
  and and_8 (and_5_out[3], B[3], SEL);
  assign M = and_1_out | and_5_out;  // OR_Gate or_1, 4 bits wide
endmodule

module _1_2_3 (
  input  A,
  input  B,
  input  C_in,
  output m0,
  output S,
  output C_out
);

  wire and_2_out, and_3_out, and_4_out, and_5_out, and_6_out, and_7_out, and_8_out, not_1_out, not_2_out,
       not_3_out;

  not not_1 (not_1_out, A);
  not not_2 (not_2_out, B);
  not not_3 (not_3_out, C_in);
  and and_1 (m0, not_3_out, not_2_out, not_1_out);
  and and_2 (and_2_out, C_in, not_2_out, not_1_out);
  and and_3 (and_3_out, not_3_out, B, not_1_out);
  and and_4 (and_4_out, C_in, B, not_1_out);
  and and_5 (and_5_out, not_3_out, not_2_out, A);
  and and_6 (and_6_out, C_in, not_2_out, A);
  and and_7 (and_7_out, not_3_out, B, A);
  and and_8 (and_8_out, C_in, B, A);
  or or_1 (S, and_2_out, and_3_out, and_5_out, and_8_out);
  or or_2 (C_out, and_4_out, and_6_out, and_7_out, and_8_out);

  // Notes on the sheet:
  //   m1
  //   m2
  //   m3
  //   m4
  //   m5
  //   m6
  //   m7
endmodule

module _1_2_4 (
  input  [3:0] A,
  input  [3:0] B,
  input  SA,
  output F,
  output [3:0] out_5
);

  wire and_1_out, and_2_out, and_3_out, and_4_out, and_5_out, and_6_out, and_7_out, and_8_out, or_1_out,
       or_2_out, or_3_out, xor_1_out, xor_3_out, xor_5_out, xor_7_out;
  wire [3:0] multiplexer_1_out, not_1_out;

  xor xor_1 (xor_1_out, A[0], multiplexer_1_out[0]);
  and and_1 (and_1_out, multiplexer_1_out[0], A[0]);
  xor xor_2 (out_5[0], xor_1_out, SA);
  and and_2 (and_2_out, xor_1_out, SA);
  Multiplexer #(.width(4), .enable("false")) multiplexer_1 (
    .in0(B), .in1(not_1_out), .out(multiplexer_1_out), .sel(SA));
  assign not_1_out = ~B;  // NOT_Gate not_1, 4 bits wide
  or or_1 (or_1_out, and_1_out, and_2_out);
  xor xor_3 (xor_3_out, A[1], multiplexer_1_out[1]);
  and and_3 (and_3_out, multiplexer_1_out[1], A[1]);
  and and_4 (and_4_out, xor_3_out, or_1_out);
  xor xor_4 (out_5[1], xor_3_out, or_1_out);
  or or_2 (or_2_out, and_3_out, and_4_out);
  xor xor_5 (xor_5_out, A[2], multiplexer_1_out[2]);
  and and_5 (and_5_out, multiplexer_1_out[2], A[2]);
  xor xor_6 (out_5[2], xor_5_out, or_2_out);
  and and_6 (and_6_out, xor_5_out, or_2_out);
  or or_3 (or_3_out, and_5_out, and_6_out);
  xor xor_7 (xor_7_out, A[3], multiplexer_1_out[3]);
  and and_7 (and_7_out, multiplexer_1_out[3], A[3]);
  xor xor_8 (out_5[3], xor_7_out, or_3_out);
  or or_4 (F, and_7_out, and_8_out);
  and and_8 (and_8_out, xor_7_out, or_3_out);
endmodule

module _1_2_5 (
  output [3:0] ABCD
);

  wire and_1_out, and_2_out, and_3_out, and_4_out, and_5_out, and_6_out, clock_1_out, decoder_1_out0,
       decoder_1_out1, decoder_1_out2, decoder_1_out3, decoder_1_out4, decoder_1_out5, decoder_1_out6,
       decoder_1_out7, decoder_1_out8, decoder_1_out9, decoder_1_out10, decoder_1_out11, decoder_1_out12,
       decoder_1_out13, decoder_1_out14, decoder_1_out15, not_1_out, not_2_out, not_3_out, not_4_out,
       not_5_out, not_6_out, not_7_out, not_8_out, not_9_out, not_10_out, not_11_out, not_12_out, not_13_out,
       not_14_out, not_15_out, not_16_out, not_17_out, not_18_out, not_19_out, not_20_out, or_2_out,
       or_3_out, or_4_out;
  wire [3:0] bitselector_1_out, bitselector_2_out, bitselector_3_out, bitselector_4_out, bitselector_5_out,
       bitselector_6_out, bitselector_7_out, bitselector_8_out, bitselector_9_out, bitselector_10_out,
       bitselector_11_out, bitselector_12_out, bitselector_13_out, bitselector_14_out, bitselector_15_out,
       bitselector_16_out, counter_1_q;

  Clock clock_1 (.out(clock_1_out));
  Decoder #(.select(4), .disabled(0), .enable("false")) decoder_1 (
    .out0(decoder_1_out0), .out1(decoder_1_out1), .out2(decoder_1_out2), .out3(decoder_1_out3),
    .out4(decoder_1_out4), .out5(decoder_1_out5), .out6(decoder_1_out6), .out7(decoder_1_out7),
    .out8(decoder_1_out8), .out9(decoder_1_out9), .out10(decoder_1_out10), .out11(decoder_1_out11),
    .out12(decoder_1_out12), .out13(decoder_1_out13), .out14(decoder_1_out14), .out15(decoder_1_out15),
    .sel(counter_1_q));
  Counter #(.width(4), .max('hf)) counter_1 (.Q(counter_1_q), .clk(clock_1_out));  // open: load, D, count, carry, clr
  not not_1 (not_1_out, decoder_1_out0);
  not not_2 (not_2_out, decoder_1_out1);
  not not_3 (not_3_out, decoder_1_out2);
  not not_4 (not_4_out, decoder_1_out3);
  not not_5 (not_5_out, decoder_1_out4);
  not not_6 (not_6_out, decoder_1_out5);
  not not_7 (not_7_out, decoder_1_out6);
  not not_8 (not_8_out, decoder_1_out7);
  not not_9 (not_9_out, decoder_1_out8);
  not not_10 (not_10_out, decoder_1_out9);
  not not_11 (not_11_out, decoder_1_out10);
  not not_12 (not_12_out, decoder_1_out11);
  not not_13 (not_13_out, decoder_1_out12);
  not not_14 (not_14_out, decoder_1_out13);
  not not_15 (not_15_out, decoder_1_out14);
  not not_16 (not_16_out, decoder_1_out15);
  BitSelector #(.width(4), .group(4)) bitselector_1 (.in(4'b0000), .out(bitselector_1_out), .sel(not_1_out));
  BitSelector #(.width(4), .group(4)) bitselector_2 (.in(4'b0001), .out(bitselector_2_out), .sel(not_2_out));
  BitSelector #(.width(4), .group(4)) bitselector_3 (.in(4'b0011), .out(bitselector_3_out), .sel(not_3_out));
  BitSelector #(.width(4), .group(4)) bitselector_4 (.in(4'b0010), .out(bitselector_4_out), .sel(not_4_out));
  BitSelector #(.width(4), .group(4)) bitselector_5 (.in(4'b0110), .out(bitselector_5_out), .sel(not_5_out));
  BitSelector #(.width(4), .group(4)) bitselector_6 (.in(4'b0111), .out(bitselector_6_out), .sel(not_6_out));
  BitSelector #(.width(4), .group(4)) bitselector_7 (.in(4'b0101), .out(bitselector_7_out), .sel(not_7_out));
  BitSelector #(.width(4), .group(4)) bitselector_8 (.in(4'b0100), .out(bitselector_8_out), .sel(not_8_out));
  BitSelector #(.width(4), .group(4)) bitselector_9 (.in(4'b1100), .out(bitselector_9_out), .sel(not_9_out));
  BitSelector #(.width(4), .group(4)) bitselector_10 (.in(4'b1101), .out(bitselector_10_out), .sel(not_10_out));
  BitSelector #(.width(4), .group(4)) bitselector_11 (.in(4'b1111), .out(bitselector_11_out), .sel(not_11_out));
  BitSelector #(.width(4), .group(4)) bitselector_12 (.in(4'b1110), .out(bitselector_12_out), .sel(not_12_out));
  BitSelector #(.width(4), .group(4)) bitselector_13 (.in(4'b1010), .out(bitselector_13_out), .sel(not_13_out));
  BitSelector #(.width(4), .group(4)) bitselector_14 (.in(4'b1011), .out(bitselector_14_out), .sel(not_14_out));
  BitSelector #(.width(4), .group(4)) bitselector_15 (.in(4'b1001), .out(bitselector_15_out), .sel(not_15_out));
  BitSelector #(.width(4), .group(4)) bitselector_16 (.in(4'b1000), .out(bitselector_16_out), .sel(not_16_out));
  assign ABCD = bitselector_1_out | bitselector_2_out | bitselector_3_out | bitselector_4_out | bitselector_5_out | bitselector_6_out | bitselector_7_out | bitselector_8_out | bitselector_9_out | bitselector_10_out | bitselector_11_out | bitselector_12_out | bitselector_13_out | bitselector_14_out | bitselector_15_out | bitselector_16_out;  // OR_Gate or_1, 4 bits wide
  not not_17 (not_17_out, ABCD[0]);
  not not_18 (not_18_out, ABCD[1]);
  or or_2 (or_2_out, ABCD[1], ABCD[0]);
  and and_1 (and_1_out, not_17_out, not_18_out, not_20_out);
  not not_19 (not_19_out, ABCD[3]);
  not not_20 (not_20_out, ABCD[2]);
  and and_2 (and_2_out, not_18_out, not_17_out, ABCD[2]);
  or or_3 (or_3_out, not_19_out, and_2_out);
  LED led_1 (.in(or_3_out));
  LED led_2 (.in(and_3_out));
  and and_3 (and_3_out, ABCD[3], and_1_out);
  LED led_3 (.in(and_4_out));
  and and_4 (and_4_out, ABCD[3], or_2_out);
  LED led_4 (.in(or_4_out));
  or or_4 (or_4_out, ABCD[3], and_1_out);
  LED led_5 (.in(and_5_out));
  and and_5 (and_5_out, not_19_out, and_2_out);
  LED led_6 (.in(and_6_out));
  and and_6 (and_6_out, not_19_out, or_2_out);

  // Notes on the sheet:
  //   D
  //   C
  //   B
  //   A
  //   Z
  //   Y
  //   X
  //   RNS
  //   YNS
  //   GNS
  //   REW
  //   YEW
  //   GEW
endmodule
