// Logisim project 5.circ as structural Verilog
module _1_2_1 (
  input  [3:0] Input_4,
  input  [3:0] Input_3,
  input  [3:0] Input_2,
  input  [3:0] Input_1,
  input  [1:0] in_5,
  output [3:0] Output
);

  wire decoder_1_out0, decoder_1_out1, decoder_1_out2, decoder_1_out3;
  wire [3:0] and_1_out, and_5_out, and_9_out, and_13_out;

  Decoder #(.select(2), .enable("false")) decoder_1 (
    .out0(decoder_1_out0), .out1(decoder_1_out1), .out2(decoder_1_out2), .out3(decoder_1_out3), .sel(in_5));
  and and_1 (and_1_out[0], Input_1[0], decoder_1_out0);
  and and_2 (and_1_out[1], Input_2[0], decoder_1_out0);
  and and_3 (and_1_out[2], Input_3[0], decoder_1_out0);
  and and_4 (and_1_out[3], Input_4[0], decoder_1_out0);
  and and_5 (and_5_out[0], Input_1[1], decoder_1_out1);
  and and_6 (and_5_out[1], Input_2[1], decoder_1_out1);
  and and_7 (and_5_out[2], Input_3[1], decoder_1_out1);
  and and_8 (and_5_out[3], Input_4[1], decoder_1_out1);
  and and_9 (and_9_out[0], Input_1[2], decoder_1_out2);
  and and_10 (and_9_out[1], Input_2[2], decoder_1_out2);
  and and_11 (and_9_out[2], Input_3[2], decoder_1_out2);
  and and_12 (and_9_out[3], Input_4[2], decoder_1_out2);
  and and_13 (and_13_out[0], Input_1[3], decoder_1_out3);
  and and_14 (and_13_out[1], Input_2[3], decoder_1_out3);
  and and_15 (and_13_out[2], Input_3[3], decoder_1_out3);
  and and_16 (and_13_out[3], Input_4[3], decoder_1_out3);
  assign Output = and_1_out | and_5_out | and_9_out | and_13_out;  // OR_Gate or_1, 4 bits wide
endmodule

module _1_2_2 (
  input  A,
  input  B,
  input  C,
  input  D,
  input  [2:0] SEL,
  input  E,
  input  F,
  input  G,
  input  H,
  output out_10
);

  wire multiplexer_1_out, multiplexer_2_out;

  Multiplexer #(.select(2), .enable("false")) multiplexer_1 (
    .in0(A), .in1(B), .in2(C), .in3(D), .out(multiplexer_1_out), .sel(SEL[1:0]));
  Multiplexer #(.select(2), .enable("false")) multiplexer_2 (
    .in0(E), .in1(F), .in2(G), .in3(H), .out(multiplexer_2_out), .sel(SEL[1:0]));
  Multiplexer #(.enable("false")) multiplexer_3 (
    .in0(multiplexer_1_out), .in1(multiplexer_2_out), .out(out_10), .sel(SEL[2]));
endmodule

module _1_2_3 (
  input  A,
  input  B,
  input  C,
  input  D,
  output F
);

  wire and_1_out, and_2_out, not_1_out, not_2_out;

  not not_1 (not_1_out, C);
  not not_2 (not_2_out, D);
  and and_1 (and_1_out, not_1_out, not_2_out);
  and and_2 (and_2_out, C, D);
  Multiplexer #(.select(2), .enable("false")) multiplexer_1 (
    .in0(D), .in1(and_1_out), .in2(and_2_out), .in3(B), .out(F), .sel({A, B}));

  // Notes on the sheet:
  //   F1
  //   F2
  //   F3
  //   F4
endmodule

module _1_2_4 (
  input  [3:0] ABCD,
  output F
);

  wire multiplexer_1_out, multiplexer_2_out, not_1_out, not_2_out, or_1_out, or_2_out;

  not not_1 (not_1_out, ABCD[1]);
  or or_1 (or_1_out, ABCD[1], not_1_out);
  not not_2 (not_2_out, ABCD[0]);
  or or_2 (or_2_out, not_2_out, ABCD[0]);
  Multiplexer #(.select(2), .enable("false")) multiplexer_1 (
    .in0(or_1_out), .in1(ABCD[1]), .in2(not_1_out), .in3(or_1_out), .out(multiplexer_1_out), .sel(ABCD[3:2]));
  Multiplexer #(.select(2), .enable("false")) multiplexer_2 (
    .in0(or_2_out), .in1(ABCD[0]), .in2(not_2_out), .in3(ABCD[0]), .out(multiplexer_2_out), .sel(ABCD[3:2]));
  and and_1 (F, multiplexer_1_out, multiplexer_2_out);

  // Notes on the sheet:
  //   C
  //   D
  //   AB
endmodule

module _1_2_5 (
  input  [2:0] in_1
);

  wire decoder_1_out1, decoder_1_out2, decoder_1_out3, decoder_1_out4, decoder_1_out5, decoder_1_out6,
       or_1_out, or_2_out, or_3_out;

  Decoder #(.select(3), .enable("false")) decoder_1 (
    .out1(decoder_1_out1), .out2(decoder_1_out2), .out3(decoder_1_out3), .out4(decoder_1_out4),
    .out5(decoder_1_out5), .out6(decoder_1_out6), .sel(in_1));  // open: out0, out7
  or or_1 (or_1_out, decoder_1_out4, decoder_1_out5, decoder_1_out6);
  or or_2 (or_2_out, decoder_1_out2, decoder_1_out3, decoder_1_out4, decoder_1_out5, decoder_1_out6);
  LED led_1 (.in(or_2_out));
  LED led_2 (.in(decoder_1_out6));
  LED led_3 (.in(or_1_out));
  or or_3 (or_3_out, decoder_1_out5, decoder_1_out3, decoder_1_out1);
  LED led_4 (.in(or_3_out));
  LED led_5 (.in(or_1_out));
  LED led_6 (.in(decoder_1_out6));
  LED led_7 (.in(or_2_out));
endmodule
