// Logisim project 6.circ as structural Verilog
module _1_2_1 (
  input  [7:0] in_1,
  input  S,
  output C,
  output [7:0] out_4
);

  wire and_1_out, and_2_out, and_3_out, and_4_out, and_5_out, and_6_out, and_7_out, and_8_out,
       multiplexer_2_out, multiplexer_3_out, multiplexer_4_out, multiplexer_5_out, multiplexer_6_out,
       multiplexer_7_out, multiplexer_8_out, or_1_out, or_2_out, or_3_out, or_4_out, or_5_out, or_6_out,
       or_7_out, or_8_out, xor_1_out, xor_2_out, xor_4_out, xor_5_out, xor_7_out, xor_8_out, xor_10_out,
       xor_11_out, xor_13_out, xor_14_out, xor_16_out, xor_17_out, xor_19_out, xor_20_out, xor_22_out,
       xor_23_out;

  and and_1 (and_1_out, xor_1_out, in_1[7]);
  Multiplexer #(.enable("false")) multiplexer_1 (.in0(and_1_out), .in1(or_1_out), .out(C), .sel(multiplexer_2_out));
  xor xor_1 (xor_1_out, S, 1'b0);
  or or_1 (or_1_out, xor_1_out, in_1[7]);
  xor xor_2 (xor_2_out, xor_1_out, in_1[7]);
  xor xor_3 (out_4[7], xor_2_out, multiplexer_2_out);
  xor xor_4 (xor_4_out, S, 1'b0);
  or or_2 (or_2_out, xor_4_out, in_1[6]);
  and and_2 (and_2_out, xor_4_out, in_1[6]);
  Multiplexer #(.enable("false")) multiplexer_2 (
    .in0(and_2_out), .in1(or_2_out), .out(multiplexer_2_out), .sel(multiplexer_3_out));
  xor xor_5 (xor_5_out, xor_4_out, in_1[6]);
  xor xor_6 (out_4[6], xor_5_out, multiplexer_3_out);
  xor xor_7 (xor_7_out, S, 1'b0);
  and and_3 (and_3_out, xor_7_out, in_1[5]);
  or or_3 (or_3_out, xor_7_out, in_1[5]);
  Multiplexer #(.enable("false")) multiplexer_3 (
    .in0(and_3_out), .in1(or_3_out), .out(multiplexer_3_out), .sel(multiplexer_4_out));
  and and_4 (and_4_out, xor_10_out, in_1[4]);
  xor xor_8 (xor_8_out, xor_7_out, in_1[5]);
  xor xor_9 (out_4[5], xor_8_out, multiplexer_4_out);
  xor xor_10 (xor_10_out, S, 1'b0);
  or or_4 (or_4_out, xor_10_out, in_1[4]);
  xor xor_11 (xor_11_out, xor_10_out, in_1[4]);
  Multiplexer #(.enable("false")) multiplexer_4 (
    .in0(and_4_out), .in1(or_4_out), .out(multiplexer_4_out), .sel(multiplexer_5_out));
  and and_5 (and_5_out, xor_13_out, in_1[3]);
  Multiplexer #(.enable("false")) multiplexer_5 (
    .in0(and_5_out), .in1(or_5_out), .out(multiplexer_5_out), .sel(multiplexer_6_out));
  xor xor_12 (out_4[4], xor_11_out, multiplexer_5_out);
  xor xor_13 (xor_13_out, S, 1'b0);
  or or_5 (or_5_out, xor_13_out, in_1[3]);
  xor xor_14 (xor_14_out, xor_13_out, in_1[3]);
  xor xor_15 (out_4[3], xor_14_out, multiplexer_6_out);
  xor xor_16 (xor_16_out, S, 1'b0);
  or or_6 (or_6_out, xor_16_out, in_1[2]);
  and and_6 (and_6_out, xor_16_out, in_1[2]);
  Multiplexer #(.enable("false")) multiplexer_6 (
    .in0(and_6_out), .in1(or_6_out), .out(multiplexer_6_out), .sel(multiplexer_7_out));
  xor xor_17 (xor_17_out, xor_16_out, in_1[2]);
  xor xor_18 (out_4[2], xor_17_out, multiplexer_7_out);
  xor xor_19 (xor_19_out, S, 1'b1);
  and and_7 (and_7_out, xor_19_out, in_1[1]);
  or or_7 (or_7_out, xor_19_out, in_1[1]);
  Multiplexer #(.enable("false")) multiplexer_7 (
    .in0(and_7_out), .in1(or_7_out), .out(multiplexer_7_out), .sel(multiplexer_8_out));
  and and_8 (and_8_out, xor_22_out, in_1[0]);
  xor xor_20 (xor_20_out, xor_19_out, in_1[1]);
  xor xor_21 (out_4[1], xor_20_out, multiplexer_8_out);
  xor xor_22 (xor_22_out, S, 1'b0);
  xor xor_23 (xor_23_out, xor_22_out, in_1[0]);
  or or_8 (or_8_out, xor_22_out, in_1[0]);
  Multiplexer #(.enable("false")) multiplexer_8 (.in0(and_8_out), .in1(or_8_out), .out(multiplexer_8_out), .sel(S));
  xor xor_24 (out_4[0], xor_23_out, S);

  // Notes on the sheet:
  //   A-in
  //   A-out
endmodule

module _1_3 (
  input  R,
  input  D,
  input  C,
  input  S,
  input  nS,
  input  nR,
  input  S_2,
  input  C_2,
  input  R_2,
  output Q,
  output Q_2,
  output nQ,
  output nQ_2,
  output Q_3,
  output nQ_3,
  output Q_4,
  output nQ_4
);

  wire nand_1_out, nand_2_out, nand_7_out, nand_8_out;

  nand nand_1 (nand_1_out, S_2, C_2);
  nand nand_2 (nand_2_out, C_2, R_2);
  nor nor_1 (Q, R, nQ);
  nor nor_2 (nQ, Q, S);
  nand nand_3 (Q_3, nS, nQ_3);
  nand nand_4 (nQ_3, Q_3, nR);
  nand nand_5 (Q_4, nand_1_out, nQ_4);
  nand nand_6 (nQ_4, Q_4, nand_2_out);
  nand nand_7 (nand_7_out, D, C);
  nand nand_8 (nand_8_out, C, ~D);  // NAND_Gate
  nand nand_9 (Q_2, nand_7_out, nQ_2);
  nand nand_10 (nQ_2, Q_2, nand_8_out);
endmodule

module _1_4_1 (
  input  D,
  input  C,
  input  D_2,
  input  C_2,
  output Q,
  output nQ,
  output Q_2,
  output nQ_2
);

  wire nand_1_out, nand_2_out, nand_3_out, nand_4_out, nand_5_out, nand_6_out, nand_7_out, nand_8_out,
       nand_9_out, nand_10_out, nand_11_out, nand_12_out, not_1_out, not_2_out, not_3_out;

  not not_1 (not_1_out, C_2);
  nand nand_1 (nand_1_out, D, C);
  nand nand_2 (nand_2_out, C, ~D);  // NAND_Gate
  nand nand_3 (nand_3_out, D_2, not_1_out);
  nand nand_4 (nand_4_out, not_1_out, ~D_2);  // NAND_Gate
  nand nand_5 (nand_5_out, nand_1_out, nand_6_out);
  nand nand_6 (nand_6_out, nand_5_out, nand_2_out);
  nand nand_7 (nand_7_out, nand_3_out, nand_8_out);
  nand nand_8 (nand_8_out, nand_7_out, nand_4_out);
  not not_2 (not_2_out, C);
  not not_3 (not_3_out, not_1_out);
  nand nand_9 (nand_9_out, nand_5_out, not_2_out);
  nand nand_10 (nand_10_out, not_2_out, nand_6_out);
  nand nand_11 (nand_11_out, nand_7_out, not_3_out);
  nand nand_12 (nand_12_out, not_3_out, nand_8_out);
  nand nand_13 (Q, nand_9_out, nQ);
  nand nand_14 (nQ, Q, nand_10_out);
  nand nand_15 (Q_2, nand_11_out, nQ_2);
  nand nand_16 (nQ_2, Q_2, nand_12_out);

  // Notes on the sheet:
  //   Q0
  //   Q0
  //   Q1
  //   Q1
endmodule

module _1_4_2 (
  input  C,
  output nA,
  output Y,
  output nB,
  output nA_2,
  output Y_2,
  output nB_2
);

  wire and_1_out, and_2_out, and_3_out, and_4_out, and_5_out, and_6_out, clock_1_out, d_ff_1_q, d_ff_2_q,
       nand_1_out, nand_2_out, nand_3_out, nand_4_out, nand_5_out, nand_6_out, nand_7_out, nand_8_out,
       nand_9_out, nand_10_out, nand_11_out, nand_12_out, nand_13_out, nand_15_out, not_1_out, not_2_out,
       not_3_out, or_1_out, or_2_out, or_3_out, or_4_out;

  and and_1 (and_1_out, nand_13_out, C);
  and and_2 (and_2_out, C, nand_15_out);
  not not_1 (not_1_out, C);
  or or_1 (or_1_out, and_1_out, and_2_out);
  and and_3 (and_3_out, nA, C);
  and and_4 (and_4_out, C, d_ff_1_q);
  and and_5 (and_5_out, C, d_ff_2_q);
  nand nand_1 (nand_1_out, or_1_out, not_1_out);
  nand nand_2 (nand_2_out, not_1_out, ~or_1_out);  // NAND_Gate
  nand nand_3 (nand_3_out, and_3_out, C);
  nand nand_4 (nand_4_out, C, ~and_3_out);  // NAND_Gate
  or or_2 (or_2_out, and_4_out, and_5_out);
  and and_6 (and_6_out, C, nA_2);
  Clock clock_1 (.out(clock_1_out));
  nand nand_5 (nand_5_out, nand_1_out, nand_6_out);
  nand nand_6 (nand_6_out, nand_5_out, nand_2_out);
  not not_2 (not_2_out, not_1_out);
  nand nand_7 (nand_7_out, nand_3_out, nand_8_out);
  nand nand_8 (nand_8_out, nand_7_out, nand_4_out);
  not not_3 (not_3_out, C);
  nand nand_9 (nand_9_out, nand_5_out, not_2_out);
  nand nand_10 (nand_10_out, not_2_out, nand_6_out);
  nand nand_11 (nand_11_out, nand_7_out, not_3_out);
  nand nand_12 (nand_12_out, not_3_out, nand_8_out);
  D_Flip_Flop d_ff_1 (.clk(clock_1_out), .D(or_2_out), .Q(d_ff_1_q), .Qn(nA_2));  // open: preset, en, reset
  D_Flip_Flop d_ff_2 (.clk(clock_1_out), .D(and_6_out), .Q(d_ff_2_q), .Qn(nB_2));  // open: preset, en, reset
  nand nand_13 (nand_13_out, nand_9_out, nA);
  nand nand_14 (nA, nand_13_out, nand_10_out);
  nand nand_15 (nand_15_out, nand_11_out, nB);
  nand nand_16 (nB, nand_15_out, nand_12_out);
  or or_3 (or_3_out, nand_13_out, nand_15_out);
  or or_4 (or_4_out, d_ff_1_q, d_ff_2_q);
  and and_7 (Y, or_3_out, not_1_out);
  and and_8 (Y_2, not_1_out, or_4_out);

  // Notes on the sheet:
  //   X
  //   DA
  //   DB
  //   DA
  //   DB
  //   A
  //   B
  //   A
  //   B
endmodule

module _1_4_3 (
  input  in_1,
  output nA,
  output Y,
  output nB
);

  wire and_1_out, and_2_out, clock_1_out, d_ff_1_q, d_ff_2_q, or_1_out;

  Clock clock_1 (.out(clock_1_out));
  and and_1 (and_1_out, nA, d_ff_2_q);
  and and_2 (and_2_out, nA, in_1);
  D_Flip_Flop d_ff_1 (.clk(clock_1_out), .D(d_ff_2_q), .Q(d_ff_1_q), .Qn(nA));  // open: preset, en, reset
  D_Flip_Flop d_ff_2 (.clk(clock_1_out), .D(or_1_out), .Q(d_ff_2_q), .Qn(nB));  // open: preset, en, reset
  or or_1 (or_1_out, and_1_out, and_2_out);
  or or_2 (Y, d_ff_1_q, d_ff_2_q, in_1);

  // Notes on the sheet:
  //   X
  //   DA
  //   DB
  //   A
  //   B
endmodule

module _1_4_4 (
  input  X,
  output A,
  output B,
  output Y
);

  wire clock_1_out, not_1_out, s_r_ff_2_qn, xor_1_out;

  Clock clock_1 (.out(clock_1_out));
  S_R_Flip_Flop s_r_ff_1 (.S(B), .clk(clock_1_out), .R(s_r_ff_2_qn), .Q(A));  // open: Qn, preset, reset, en
  xor xor_1 (xor_1_out, A, X);
  not not_1 (not_1_out, xor_1_out);
  S_R_Flip_Flop s_r_ff_2 (
    .S(not_1_out), .clk(clock_1_out), .R(xor_1_out), .Q(B), .Qn(s_r_ff_2_qn));  // open: preset, reset, en
  xor xor_2 (Y, B, xor_1_out);

  // Notes on the sheet:
  //   Sa
  //   Ra
  //   Sb
  //   Rb
endmodule
