// Logisim project 7.circ as structural Verilog
module _1_1 (
  input  P0,
  input  P1,
  input  P2,
  input  P3,
  input  S,
  input  D_S,
  output Q0,
  output Q1,
  output Q2,
  output out_10
);

  wire and_1_out, and_2_out, and_3_out, and_4_out, and_5_out, and_6_out, and_7_out, and_8_out, and_9_out,
       and_10_out, clock_1_out, clock_2_out, nor_1_out, nor_2_out, nor_3_out, nor_4_out, not_1_out,
       not_2_out, not_3_out, not_4_out, not_5_out, not_6_out, not_7_out, not_8_out, not_9_out, not_10_out,
       or_1_out;

  Clock clock_1 (.out(clock_1_out));
  Clock clock_2 (.out(clock_2_out));
  not not_1 (not_1_out, S);
  not not_2 (not_2_out, not_1_out);
  and and_1 (and_1_out, not_1_out, clock_1_out);
  and and_2 (and_2_out, D_S, not_1_out);
  or or_1 (or_1_out, and_1_out, and_3_out);
  and and_3 (and_3_out, S, clock_2_out);
  and and_4 (and_4_out, not_2_out, P0);
  nor nor_1 (nor_1_out, and_2_out, and_4_out);
  not not_3 (not_3_out, nor_1_out);
  not not_4 (not_4_out, or_1_out);
  S_R_Flip_Flop s_r_ff_1 (.S(not_3_out), .clk(not_4_out), .R(nor_1_out), .Q(Q0));  // open: Qn, preset, reset, en
  and and_5 (and_5_out, Q0, not_1_out);
  and and_6 (and_6_out, not_2_out, P1);
  nor nor_2 (nor_2_out, and_5_out, and_6_out);
  not not_5 (not_5_out, nor_2_out);
  S_R_Flip_Flop s_r_ff_2 (.S(not_5_out), .clk(not_6_out), .R(nor_2_out), .Q(Q1));  // open: Qn, preset, reset, en
  not not_6 (not_6_out, or_1_out);
  and and_7 (and_7_out, Q1, not_1_out);
  nor nor_3 (nor_3_out, and_7_out, and_8_out);
  and and_8 (and_8_out, not_2_out, P2);
  not not_7 (not_7_out, nor_3_out);
  not not_8 (not_8_out, or_1_out);
  and and_9 (and_9_out, Q2, not_1_out);
  S_R_Flip_Flop s_r_ff_3 (.S(not_7_out), .clk(not_8_out), .R(nor_3_out), .Q(Q2));  // open: Qn, preset, reset, en
  and and_10 (and_10_out, not_2_out, P3);
  nor nor_4 (nor_4_out, and_9_out, and_10_out);
  not not_9 (not_9_out, nor_4_out);
  not not_10 (not_10_out, or_1_out);
  S_R_Flip_Flop s_r_ff_4 (.S(not_9_out), .clk(not_10_out), .R(nor_4_out), .Q(out_10));  // open: Qn, preset, reset, en

  // Notes on the sheet:
  //   ~CP1
  //   ~CP2
  //   Q3
endmodule

module _1_2 (
  input  X,
  output A,
  output B,
  output C,
  output Y
);

  wire and_1_out, and_2_out, and_3_out, and_4_out, and_5_out, and_6_out, and_7_out, and_8_out, and_9_out,
       and_10_out, and_11_out, and_12_out, and_13_out, clock_1_out, d_ff_1_qn, d_ff_2_qn, d_ff_3_qn,
       not_1_out, or_1_out, or_2_out, or_3_out;

  not not_1 (not_1_out, X);
  and and_1 (and_1_out, A, d_ff_3_qn, d_ff_2_qn);
  and and_2 (and_2_out, X, d_ff_2_qn);
  and and_3 (and_3_out, not_1_out, C);
  and and_4 (and_4_out, B, C);
  and and_5 (and_5_out, A, C);
  and and_6 (and_6_out, d_ff_2_qn, d_ff_3_qn, not_1_out);
  and and_7 (and_7_out, A, d_ff_2_qn, d_ff_3_qn);
  and and_8 (and_8_out, d_ff_1_qn, d_ff_2_qn, C);
  and and_9 (and_9_out, d_ff_1_qn, d_ff_2_qn, not_1_out);
  and and_10 (and_10_out, d_ff_1_qn, B, X);
  and and_11 (and_11_out, A, B, not_1_out);
  and and_12 (and_12_out, d_ff_2_qn, not_1_out);
  or or_1 (or_1_out, and_1_out, and_2_out);
  or or_2 (or_2_out, and_3_out, and_4_out, and_5_out);
  Clock clock_1 (.out(clock_1_out));
  or or_3 (or_3_out, and_6_out, and_7_out, and_8_out);
  and and_13 (and_13_out, A, d_ff_2_qn, d_ff_3_qn, X);
  D_Flip_Flop d_ff_1 (.clk(clock_1_out), .D(or_1_out), .Q(A), .Qn(d_ff_1_qn));  // open: preset, en, reset
  D_Flip_Flop d_ff_2 (.clk(clock_1_out), .D(or_2_out), .Q(B), .Qn(d_ff_2_qn));  // open: preset, en, reset
  D_Flip_Flop d_ff_3 (.clk(clock_1_out), .D(or_3_out), .Q(C), .Qn(d_ff_3_qn));  // open: preset, en, reset
  or or_4 (Y, and_9_out, and_10_out, and_11_out, and_12_out, and_13_out);

  // Notes on the sheet:
  //   SA
  //   SB
  //   SC
endmodule

module _1_3 (
  input  [3:0] IN,
  input  CLK,
  input  SH,
  output A,
  output B,
  output C,
  output [3:0] out_7
);

  wire and_1_out, and_2_out, and_3_out, and_4_out, and_5_out, and_6_out, and_7_out, and_8_out, and_9_out,
       and_10_out, and_11_out, and_12_out, and_13_out, clock_1_out, d_ff_1_qn, d_ff_2_qn, d_ff_3_qn,
       not_1_out, not_2_out, or_1_out, or_2_out, or_3_out, or_4_out, shift_register_1_out;

  not not_1 (not_1_out, SH);
  Shift_Register #(.length(4)) shift_register_1 (
    .shift(SH), .in(1'b0), .clk(CLK), .out(shift_register_1_out), .load(not_1_out), .d0(IN[3]), .d1(IN[2]),
    .d2(IN[1]), .d3(IN[0]));  // open: clr, q0, q1, q2, q3
  not not_2 (not_2_out, shift_register_1_out);
  and and_1 (and_1_out, A, d_ff_3_qn, d_ff_2_qn);
  and and_2 (and_2_out, shift_register_1_out, d_ff_2_qn);
  and and_3 (and_3_out, not_2_out, C);
  and and_4 (and_4_out, B, C);
  and and_5 (and_5_out, A, C);
  and and_6 (and_6_out, d_ff_2_qn, d_ff_3_qn, not_2_out);
  and and_7 (and_7_out, A, d_ff_2_qn, d_ff_3_qn);
  and and_8 (and_8_out, d_ff_1_qn, d_ff_2_qn, C);
  and and_9 (and_9_out, d_ff_1_qn, d_ff_2_qn, not_2_out);
  and and_10 (and_10_out, d_ff_1_qn, B, shift_register_1_out);
  and and_11 (and_11_out, A, B, not_2_out);
  and and_12 (and_12_out, d_ff_2_qn, not_2_out);
  or or_1 (or_1_out, and_1_out, and_2_out);
  or or_2 (or_2_out, and_3_out, and_4_out, and_5_out);
  Clock clock_1 (.out(clock_1_out));
  or or_3 (or_3_out, and_6_out, and_7_out, and_8_out);
  and and_13 (and_13_out, A, d_ff_2_qn, d_ff_3_qn, shift_register_1_out);
  D_Flip_Flop d_ff_1 (.clk(clock_1_out), .D(or_1_out), .Q(A), .Qn(d_ff_1_qn));  // open: preset, en, reset
  D_Flip_Flop d_ff_2 (.clk(clock_1_out), .D(or_2_out), .Q(B), .Qn(d_ff_2_qn));  // open: preset, en, reset
  D_Flip_Flop d_ff_3 (.clk(clock_1_out), .D(or_3_out), .Q(C), .Qn(d_ff_3_qn));  // open: preset, en, reset
  or or_4 (or_4_out, and_9_out, and_10_out, and_11_out, and_12_out, and_13_out);
  Shift_Register #(.length(4)) shift_register_2 (
    .shift(SH), .in(or_4_out), .clk(CLK), .q0(out_7[3]), .q1(out_7[2]), .q2(out_7[1]), .q3(out_7[0]));  // open: out, load, clr, d0, d1, d2, d3

  // Notes on the sheet:
  //   X
  //   SA
  //   SB
  //   SC
  //   Y
  //   OUT
endmodule
