// Logisim project 8.circ as structural Verilog
module _1_1_4 (
  input  D,
  input  N,
  output P,
  output H
);

  wire and_1_out, and_2_out, and_3_out, and_4_out, and_5_out, and_6_out, and_7_out, buffer_1_out,
       buffer_2_out, buffer_3_out, buffer_4_out, d_ff_1_q, d_ff_1_qn, d_ff_2_q, d_ff_2_qn, not_1_out,
       not_2_out, or_1_out, or_2_out, or_3_out;

  not not_1 (not_1_out, D);
  not not_2 (not_2_out, N);
  and and_1 (and_1_out, d_ff_1_q, not_1_out, not_2_out);
  and and_2 (and_2_out, N, d_ff_2_q, d_ff_1_qn);
  and and_3 (and_3_out, D, d_ff_2_qn);
  and and_4 (and_4_out, d_ff_1_qn, N);
  and and_5 (and_5_out, d_ff_2_q, not_2_out, not_1_out);
  or or_1 (or_1_out, and_1_out, and_2_out, and_3_out);
  or or_2 (or_2_out, and_3_out, and_4_out, and_5_out);
  or or_3 (or_3_out, N, D);
  buf buffer_1 (buffer_1_out, buffer_3_out);
  buf buffer_2 (buffer_2_out, buffer_1_out);
  buf buffer_3 (buffer_3_out, or_3_out);
  buf buffer_4 (buffer_4_out, buffer_2_out);
  D_Flip_Flop d_ff_1 (.clk(buffer_4_out), .D(or_1_out), .Q(d_ff_1_q), .Qn(d_ff_1_qn));  // open: preset, en, reset
  D_Flip_Flop d_ff_2 (.clk(buffer_4_out), .D(or_2_out), .Q(d_ff_2_q), .Qn(d_ff_2_qn));  // open: preset, en, reset
  and and_6 (and_6_out, d_ff_1_q, N);
  and and_7 (and_7_out, d_ff_2_q, D);
  and and_8 (H, d_ff_1_q, D);
  or or_4 (P, and_6_out, and_7_out);

  // Notes on the sheet:
  //   S1'
  //   S2'
  //   S1
  //   S2
endmodule

module _2 (
  input  X9,
  input  X8,
  input  X7,
  input  X6,
  input  X5,
  input  X4,
  input  X3,
  input  X2,
  input  X1,
  input  X0,
  input  [7:0] in_11,
  input  in_12,
  output Y,
  output [7:0] out_14
);

  wire and_1_out, and_2_out, and_3_out, and_5_out, and_6_out, buffer_1_out, buffer_2_out, buffer_3_out,
       buffer_4_out, buffer_5_out, buffer_6_out, d_ff_1_q, d_ff_1_qn, d_ff_2_qn, d_ff_3_q, d_ff_3_qn,
       or_1_out, or_2_out, or_3_out, or_4_out, or_5_out, or_6_out, xnor_1_out, xnor_2_out, xnor_3_out,
       xnor_4_out;
  wire [1:0] d_ff_2_q;
  wire [3:0] rom_1_data;

  xor xor_1 (d_ff_2_q[1], d_ff_2_q[0], d_ff_3_q);
  or or_1 (or_1_out, X1, X3, X5, X7, X9);
  or or_2 (or_2_out, X2, X3, X6, X7);
  or or_3 (or_3_out, X4, X5, X6, X7);
  or or_4 (or_4_out, X8, X9);
  or or_5 (or_5_out, X0, X1, X2, X3, X4, X5, X6, X7, X8, X9);
  ROM #(.addrWidth(2), .dataWidth(4)) rom_1 (.addr(d_ff_2_q), .data(rom_1_data), .sel(in_12));
  xnor xnor_1 (xnor_1_out, or_1_out, rom_1_data[0]);
  xnor xnor_2 (xnor_2_out, or_2_out, rom_1_data[1]);
  xnor xnor_3 (xnor_3_out, or_3_out, rom_1_data[2]);
  xnor xnor_4 (xnor_4_out, or_4_out, rom_1_data[3]);
  and and_1 (and_1_out, xnor_1_out, xnor_2_out, xnor_3_out, xnor_4_out);
  and and_2 (and_2_out, and_1_out, d_ff_3_q);
  and and_3 (and_3_out, d_ff_1_qn, d_ff_2_q[0], and_1_out);
  buf buffer_1 (buffer_1_out, buffer_2_out);
  buf buffer_2 (buffer_2_out, or_5_out);
  and and_4 (Y, and_1_out, d_ff_1_q);
  and and_5 (and_5_out, and_1_out, d_ff_3_qn, d_ff_2_q[0], d_ff_1_qn);
  or or_6 (or_6_out, and_2_out, and_3_out);
  and and_6 (and_6_out, d_ff_2_qn, and_1_out);
  buf buffer_3 (buffer_3_out, buffer_5_out);
  buf buffer_4 (buffer_4_out, buffer_1_out);
  buf buffer_5 (buffer_5_out, buffer_4_out);
  buf buffer_6 (buffer_6_out, buffer_3_out);
  D_Flip_Flop d_ff_1 (.clk(buffer_6_out), .D(and_5_out), .Q(d_ff_1_q), .Qn(d_ff_1_qn));  // open: preset, en, reset
  D_Flip_Flop d_ff_2 (.clk(buffer_6_out), .D(or_6_out), .Q(d_ff_2_q[0]), .Qn(d_ff_2_qn));  // open: preset, en, reset
  D_Flip_Flop d_ff_3 (.clk(buffer_6_out), .D(and_6_out), .Q(d_ff_3_q), .Qn(d_ff_3_qn));  // open: preset, en, reset

  // Notes on the sheet:
  //   Xd
  //   Xc
  //   Xb
  //   Xa
  //   contents of rom_1 (hex, n*v repeats v):
  //   1 2 3 4
  //   X
  //   DA
  //   DB
  //   DC
  //   A
  //   B
  //   C
endmodule

module _3 (
  input  LEFT,
  input  HAZ,
  input  RIGHT,
  output RC,
  output RB,
  output RA,
  output LA,
  output LB,
  output LC
);

  wire and_1_out, and_2_out, and_3_out, and_4_out, and_5_out, and_6_out, and_7_out, and_8_out, clock_1_out,
       d_ff_1_q, d_ff_1_qn, d_ff_2_q, d_ff_2_qn, d_ff_3_q, d_ff_3_qn, d_ff_4_q, d_ff_4_qn, not_1_out,
       not_2_out, or_1_out, or_2_out, or_3_out, or_4_out;

  not not_1 (not_1_out, RIGHT);
  not not_2 (not_2_out, LEFT);
  and and_1 (and_1_out, LEFT, not_1_out);
  and and_2 (and_2_out, not_2_out, RIGHT);
  and and_3 (and_3_out, d_ff_1_qn, and_1_out);
  or or_1 (or_1_out, and_3_out, and_4_out);
  and and_4 (and_4_out, d_ff_2_q, d_ff_1_qn);
  and and_5 (and_5_out, d_ff_3_qn, and_2_out);
  or or_2 (or_2_out, and_5_out, and_6_out);
  and and_6 (and_6_out, d_ff_4_q, d_ff_3_qn);
  Clock clock_1 (.out(clock_1_out));
  D_Flip_Flop d_ff_1 (.clk(clock_1_out), .D(d_ff_2_q), .Q(d_ff_1_q), .Qn(d_ff_1_qn));  // open: preset, en, reset
  D_Flip_Flop d_ff_2 (.clk(clock_1_out), .D(or_1_out), .Q(d_ff_2_q), .Qn(d_ff_2_qn));  // open: preset, en, reset
  D_Flip_Flop d_ff_3 (.clk(clock_1_out), .D(d_ff_4_q), .Q(d_ff_3_q), .Qn(d_ff_3_qn));  // open: preset, en, reset
  D_Flip_Flop d_ff_4 (.clk(clock_1_out), .D(or_2_out), .Q(d_ff_4_q), .Qn(d_ff_4_qn));  // open: preset, en, reset
  and and_7 (and_7_out, d_ff_1_q, d_ff_2_qn);
  or or_3 (or_3_out, d_ff_1_q, d_ff_2_q);
  and and_8 (and_8_out, d_ff_3_q, d_ff_4_qn);
  or or_4 (or_4_out, d_ff_3_q, d_ff_4_q);
  or or_5 (RC, and_7_out, HAZ);
  or or_6 (RB, d_ff_1_q, HAZ);
  or or_7 (RA, or_3_out, HAZ);
  or or_8 (LA, HAZ, or_4_out);
  or or_9 (LB, HAZ, d_ff_3_q);
  or or_10 (LC, HAZ, and_8_out);

  // Notes on the sheet:
  //   DB
  //   DA
  //   DB
  //   DA
  //   A
  //   B
  //   A
  //   B
endmodule
