// Logisim project Gray.circ as structural Verilog: 1 circuit, main circuit main
module main (
  output [3:0] out_1
);

  wire clock_1_out, decoder_1_out0, decoder_1_out1, decoder_1_out2, decoder_1_out3, decoder_1_out4,
       decoder_1_out5, decoder_1_out6, decoder_1_out7, decoder_1_out8, decoder_1_out9, decoder_1_out10,
       decoder_1_out11, decoder_1_out12, decoder_1_out13, decoder_1_out14, decoder_1_out15, not_1_out,
       not_2_out, not_3_out, not_4_out, not_5_out, not_6_out, not_7_out, not_8_out, not_9_out, not_10_out,
       not_11_out, not_12_out, not_13_out, not_14_out, not_15_out, not_16_out;
  wire [3:0] bitselector_1_out, bitselector_2_out, bitselector_3_out, bitselector_4_out, bitselector_5_out,
       bitselector_6_out, bitselector_7_out, bitselector_8_out, bitselector_9_out, bitselector_10_out,
       bitselector_11_out, bitselector_12_out, bitselector_13_out, bitselector_14_out, bitselector_15_out,
       bitselector_16_out, counter_1_q;

  Counter #(.width(4), .max('hf)) counter_1 (.Q(counter_1_q), .clk(clock_1_out));  // open: load, D, count, carry, clr
  Clock clock_1 (.out(clock_1_out));
  Decoder #(.select(4), .disabled(0), .enable("false")) decoder_1 (
    .out0(decoder_1_out0), .out1(decoder_1_out1), .out2(decoder_1_out2), .out3(decoder_1_out3),
    .out4(decoder_1_out4), .out5(decoder_1_out5), .out6(decoder_1_out6), .out7(decoder_1_out7),
    .out8(decoder_1_out8), .out9(decoder_1_out9), .out10(decoder_1_out10), .out11(decoder_1_out11),
    .out12(decoder_1_out12), .out13(decoder_1_out13), .out14(decoder_1_out14), .out15(decoder_1_out15),
    .sel(counter_1_q));
  not not_1 (not_1_out, decoder_1_out0);
  not not_2 (not_2_out, decoder_1_out1);
  not not_3 (not_3_out, decoder_1_out2);
  not not_4 (not_4_out, decoder_1_out3);
  not not_5 (not_5_out, decoder_1_out4);
  not not_6 (not_6_out, decoder_1_out5);
  not not_7 (not_7_out, decoder_1_out6);
  not not_8 (not_8_out, decoder_1_out7);
  not not_9 (not_9_out, decoder_1_out8);
  not not_10 (not_10_out, decoder_1_out9);
  not not_11 (not_11_out, decoder_1_out10);
  not not_12 (not_12_out, decoder_1_out11);
  not not_13 (not_13_out, decoder_1_out12);
  not not_14 (not_14_out, decoder_1_out13);
  not not_15 (not_15_out, decoder_1_out14);
  not not_16 (not_16_out, decoder_1_out15);
  BitSelector #(.width(4), .group(4)) bitselector_1 (.in(4'b0000), .out(bitselector_1_out), .sel(not_1_out));
  BitSelector #(.width(4), .group(4)) bitselector_2 (.in(4'b0001), .out(bitselector_2_out), .sel(not_2_out));
  BitSelector #(.width(4), .group(4)) bitselector_3 (.in(4'b0011), .out(bitselector_3_out), .sel(not_3_out));
  BitSelector #(.width(4), .group(4)) bitselector_4 (.in(4'b0010), .out(bitselector_4_out), .sel(not_4_out));
  BitSelector #(.width(4), .group(4)) bitselector_5 (.in(4'b0110), .out(bitselector_5_out), .sel(not_5_out));
  BitSelector #(.width(4), .group(4)) bitselector_6 (.in(4'b0111), .out(bitselector_6_out), .sel(not_6_out));
  BitSelector #(.width(4), .group(4)) bitselector_7 (.in(4'b0101), .out(bitselector_7_out), .sel(not_7_out));
  BitSelector #(.width(4), .group(4)) bitselector_8 (.in(4'b0100), .out(bitselector_8_out), .sel(not_8_out));
  BitSelector #(.width(4), .group(4)) bitselector_9 (.in(4'b1100), .out(bitselector_9_out), .sel(not_9_out));
  BitSelector #(.width(4), .group(4)) bitselector_10 (.in(4'b1101), .out(bitselector_10_out), .sel(not_10_out));
  BitSelector #(.width(4), .group(4)) bitselector_11 (.in(4'b1111), .out(bitselector_11_out), .sel(not_11_out));
  BitSelector #(.width(4), .group(4)) bitselector_12 (.in(4'b1110), .out(bitselector_12_out), .sel(not_12_out));
  BitSelector #(.width(4), .group(4)) bitselector_13 (.in(4'b1010), .out(bitselector_13_out), .sel(not_13_out));
  BitSelector #(.width(4), .group(4)) bitselector_14 (.in(4'b1011), .out(bitselector_14_out), .sel(not_14_out));
  BitSelector #(.width(4), .group(4)) bitselector_15 (.in(4'b1001), .out(bitselector_15_out), .sel(not_15_out));
  BitSelector #(.width(4), .group(4)) bitselector_16 (.in(4'b1000), .out(bitselector_16_out), .sel(not_16_out));
  assign out_1 = bitselector_1_out | bitselector_2_out | bitselector_3_out | bitselector_4_out | bitselector_5_out | bitselector_6_out | bitselector_7_out | bitselector_8_out | bitselector_9_out | bitselector_10_out | bitselector_11_out | bitselector_12_out | bitselector_13_out | bitselector_14_out | bitselector_15_out | bitselector_16_out;  // OR_Gate or_1, 4 bits wide
endmodule
